// Logisim project MajchrowskiMateuszD2T.circ as structural Verilog: 1 circuit, main circuit main
// T
module main (
  input  Reset,
  input  nCLK,
  input  T,
  output out_4,
  output out_5
);

  wire nor_1_out, nor_2_out, nor_3_out, nor_4_out, nor_5_out, nor_6_out, nor_7_out, nor_8_out, nor_9_out,
       nor_10_out;

  nor nor_1 (nor_1_out, T, nor_4_out);
  nor nor_2 (nor_2_out, nor_1_out, nor_3_out);
  nor nor_3 (nor_3_out, nor_4_out, out_5);
  nor nor_4 (nor_4_out, T, out_5);
  nor nor_5 (nor_5_out, nor_2_out, ~nCLK);  // NOR_Gate
  nor nor_6 (nor_6_out, ~nCLK, ~nor_2_out);  // NOR_Gate
  nor nor_7 (nor_7_out, nor_5_out, nor_8_out);
  nor nor_8 (nor_8_out, nor_7_out, nor_6_out);
  nor nor_9 (nor_9_out, nor_7_out, nCLK);
  nor Q (out_4, nor_9_out, out_5);
  nor nQ (out_5, out_4, nor_10_out);
  nor nor_10 (nor_10_out, nCLK, ~nor_7_out);  // NOR_Gate

  // Notes on the sheet:
  //   XNOR
  //   W przypadku nie działania schematu  odłączyć bramke x i podłączyć przycisk RESET
  //   D-aktywowany p.wysokim
  //   RE
  //   2x flip flop D
  //   D- aktywowany p.niskim
  //   FE
endmodule
