// Logisim project MajchrowskiMateuszC167.circ as structural Verilog: 1 circuit, main circuit main
module main (
  input  nCP0,
  output _1,
  output _2,
  output _4,
  output _8,
  output _16,
  output _32,
  output _64,
  output _128
);

  wire and_1_out, MR_2_out, MR_out;

  T_Flip_Flop #(.trigger("falling")) t_ff_1 (.clk(nCP0), .T(1'b1), .Q(_1), .reset(MR_out));  // open: Qn, preset, en
  T_Flip_Flop #(.trigger("falling")) t_ff_2 (.clk(_1), .T(1'b1), .Q(_2), .reset(MR_out));  // open: Qn, preset, en
  T_Flip_Flop #(.trigger("falling")) t_ff_3 (.clk(_2), .T(1'b1), .Q(_4), .reset(MR_out));  // open: Qn, preset, en
  and MR (MR_out, _128, and_1_out);
  T_Flip_Flop #(.trigger("falling")) t_ff_4 (.clk(_4), .T(1'b1), .Q(_8), .reset(MR_out));  // open: Qn, preset, en
  and and_1 (and_1_out, _4, _2, _1, _32);
  T_Flip_Flop #(.trigger("falling")) t_ff_5 (.clk(_8), .T(1'b1), .Q(_16), .reset(MR_2_out));  // open: Qn, preset, en
  and MR_2 (MR_2_out, and_1_out, _128);
  T_Flip_Flop #(.trigger("falling")) t_ff_6 (.clk(_16), .T(1'b1), .Q(_32), .reset(MR_2_out));  // open: Qn, preset, en
  T_Flip_Flop #(.trigger("falling")) t_ff_7 (.clk(_32), .T(1'b1), .Q(_64), .reset(MR_2_out));  // open: Qn, preset, en
  T_Flip_Flop #(.trigger("falling")) t_ff_8 (.clk(_64), .T(1'b1), .Q(_128), .reset(MR_2_out));  // open: Qn, preset, en

  // Notes on the sheet:
  //   MODULO 167
  //   /CP1
  //   MR1
  //   /CP0
  //   MR2
  //   MR1
  //   /CP1
  //   MR2
endmodule
