// Logisim project MajchrowskiMateuszALU.circ as structural Verilog: 1 circuit, main circuit main
module main (
  input  C,
  input  B0,
  input  A0,
  input  B1,
  input  A1,
  input  [1:0] F,
  output out_7,
  output out_8,
  output out_9,
  output ALU0,
  output out_11,
  output out_12,
  output out_13,
  output out_14,
  output ALU1,
  output out_16,
  output out_17
);

  wire and_2_out, and_3_out, and_5_out, and_6_out, C_out;

  xor XOR (out_8, B0, A0);
  nor NOR (out_9, B0, A0);
  and AND (out_11, B0, A0);
  and and_2 (and_2_out, A0, C);
  and and_3 (and_3_out, B0, C);
  xor XOR_2 (out_13, B1, A1);
  nor NOR_2 (out_14, B1, A1);
  and AND_4 (out_16, B1, A1);
  and and_5 (and_5_out, A1, C_out);
  and and_6 (and_6_out, B1, C_out);
  xor S (out_7, C, out_8);
  or u_C (C_out, out_11, and_2_out, and_3_out);
  xor S_2 (out_12, C_out, out_13);
  or C_2 (out_17, out_16, and_5_out, and_6_out);
  Multiplexer #(.select(2)) multiplexer_1 (
    .in0(out_7), .in1(out_8), .in2(out_9), .in3(out_11), .out(ALU0), .sel(F));  // open: en
  Multiplexer #(.select(2)) multiplexer_2 (
    .in0(out_12), .in1(out_13), .in2(out_14), .in3(out_16), .out(ALU1), .sel(F));  // open: en
endmodule
