// Logisim project MajchrowskiMateuszZ80.circ as structural Verilog: 1 circuit, main circuit main
module main (
  input  in_1,
  input  nM1,
  input  nIORQ,
  input  CLK_star,
  input  nMREQ,
  input  nWR,
  input  [1:0] F,
  input  nMREQ_2,
  input  nIORQ_2,
  input  nWR_2,
  input  nRD,
  output out_12,
  output nMWR,
  output nMRD,
  output nIOWR,
  output nIORD
);

  wire multiplexer_1_out, nor_1_out, nor_2_out, RE_2_q, RE_2_qn, RE_3_q, RE_4_q, RE_5_q, RE_qn;

  D_Flip_Flop RE (.clk(in_1), .D(1'b1), .Qn(RE_qn), .reset(nor_1_out));  // open: Q, preset, en
  nor nor_1 (nor_1_out, nM1, nIORQ);
  nor nor_2 (nor_2_out, nMREQ, nWR);
  D_Flip_Flop RE_2 (.clk(CLK_star), .D(nor_2_out), .Q(RE_2_q), .Qn(RE_2_qn));  // open: preset, en, reset
  D_Flip_Flop RE_3 (.clk(CLK_star), .D(RE_2_q), .Q(RE_3_q));  // open: Qn, preset, en, reset
  or or_1 (nMWR, nMREQ_2, nWR_2);
  or or_2 (nMRD, nMREQ_2, nRD);
  or or_3 (nIOWR, nIORQ_2, nWR_2);
  or or_4 (nIORD, nIORQ_2, nRD);
  D_Flip_Flop RE_4 (.clk(CLK_star), .D(RE_3_q), .Q(RE_4_q));  // open: Qn, preset, en, reset
  D_Flip_Flop RE_5 (.clk(CLK_star), .D(RE_4_q), .Q(RE_5_q));  // open: Qn, preset, en, reset
  Multiplexer #(.select(2)) multiplexer_1 (
    .in0(RE_2_q), .in1(RE_3_q), .in2(RE_4_q), .in3(RE_5_q), .out(multiplexer_1_out), .sel(F));  // open: en
  or or_5 (out_12, multiplexer_1_out, RE_2_qn);

  // Notes on the sheet:
  //   /WAIT
endmodule
