// Logisim project MajchrowskiMateuszKBD.circ as structural Verilog: 1 circuit, main circuit main
module main (
  input  nWR,
  input  nIORQ,
  input  nRD,
  input  Keyboard_Selected,
  input  D3,
  input  D2,
  input  D1,
  input  D0,
  input  in_9,
  input  in_10,
  input  in_11,
  input  in_12,
  input  in_13,
  input  in_14,
  input  in_15,
  input  in_16,
  input  in_17,
  input  in_18,
  input  in_19,
  input  in_20,
  input  in_21,
  input  in_22,
  input  in_23,
  input  in_24,
  output D3_2,
  output D2_2,
  output D1_2,
  output D0_2
);

  wire and_1_out, and_2_out, buffer_1_out, buffer_2_out, buffer_3_out, buffer_4_out, nor_1_out, nor_2_out,
       transistor_1_out, transistor_2_out, transistor_3_out, transistor_4_out;
  wire [3:0] register_1_q;

  assign D3_2 = and_1_out ? transistor_1_out : 1'bz;  // Controlled_Buffer controlled_buffer_1
  assign D2_2 = and_1_out ? transistor_2_out : 1'bz;  // Controlled_Buffer controlled_buffer_2
  assign D1_2 = and_1_out ? transistor_3_out : 1'bz;  // Controlled_Buffer controlled_buffer_3
  assign D0_2 = and_1_out ? transistor_4_out : 1'bz;  // Controlled_Buffer controlled_buffer_4
  nor nor_1 (nor_1_out, nWR, nIORQ);
  nor nor_2 (nor_2_out, nIORQ, nRD);
  and and_1 (and_1_out, nor_2_out, Keyboard_Selected);
  and and_2 (and_2_out, Keyboard_Selected, nor_1_out);
  Register #(.width(4)) register_1 (.D({D3, D2, D1, D0}), .Q(register_1_q), .clk(and_2_out));  // open: en, clr
  buf buffer_1 (buffer_1_out, register_1_q[0]);
  Transistor #(.\type ("n")) transistor_1 (.in(buffer_1_out), .out(transistor_1_out), .gate(in_9));
  Transistor #(.\type ("n")) transistor_2 (.in(buffer_1_out), .out(transistor_2_out), .gate(in_13));
  Transistor #(.\type ("n")) transistor_3 (.in(buffer_1_out), .out(transistor_3_out), .gate(in_17));
  Transistor #(.\type ("n")) transistor_4 (.in(buffer_1_out), .out(transistor_4_out), .gate(in_21));
  buf buffer_2 (buffer_2_out, register_1_q[1]);
  Transistor #(.\type ("n")) transistor_5 (.in(buffer_2_out), .out(transistor_1_out), .gate(in_10));
  Transistor #(.\type ("n")) transistor_6 (.in(buffer_2_out), .out(transistor_2_out), .gate(in_14));
  Transistor #(.\type ("n")) transistor_7 (.in(buffer_2_out), .out(transistor_3_out), .gate(in_18));
  Transistor #(.\type ("n")) transistor_8 (.in(buffer_2_out), .out(transistor_4_out), .gate(in_22));
  buf buffer_3 (buffer_3_out, register_1_q[2]);
  Transistor #(.\type ("n")) transistor_9 (.in(buffer_4_out), .out(transistor_1_out), .gate(in_12));
  Transistor #(.\type ("n")) transistor_10 (.in(buffer_3_out), .out(transistor_1_out), .gate(in_11));
  Transistor #(.\type ("n")) transistor_11 (.in(buffer_3_out), .out(transistor_2_out), .gate(in_15));
  Transistor #(.\type ("n")) transistor_12 (.in(buffer_4_out), .out(transistor_2_out), .gate(in_16));
  Transistor #(.\type ("n")) transistor_13 (.in(buffer_3_out), .out(transistor_3_out), .gate(in_19));
  Transistor #(.\type ("n")) transistor_14 (.in(buffer_4_out), .out(transistor_3_out), .gate(in_20));
  Transistor #(.\type ("n")) transistor_15 (.in(buffer_3_out), .out(transistor_4_out), .gate(in_23));
  Transistor #(.\type ("n")) transistor_16 (.in(buffer_4_out), .out(transistor_4_out), .gate(in_24));
  buf buffer_4 (buffer_4_out, register_1_q[3]);
  Pull_Resistor #(.pull(1)) pull_resistor_1 (.node(transistor_1_out));
  Pull_Resistor #(.pull(1)) pull_resistor_2 (.node(transistor_2_out));
  Pull_Resistor #(.pull(1)) pull_resistor_3 (.node(transistor_3_out));
  Pull_Resistor #(.pull(1)) pull_resistor_4 (.node(transistor_4_out));

  // Notes on the sheet:
  //   IOWR
  //   IORD
  //   KBDRD
  //   buffer_1 drives only 0 and floats otherwise
  //   KBDWR
  //   buffer_2 drives only 0 and floats otherwise
  //   buffer_3 drives only 0 and floats otherwise
  //   0/floating
  //   buffer_4 drives only 0 and floats otherwise
endmodule
