// Logisim project MajchrowskiMateuszBCD.circ as structural Verilog: 1 circuit, main circuit main
module main (
  input  [3:0] in_1
);

  wire A_out, B_out, C_out, D_out, decoder_1_out0, decoder_1_out1, decoder_1_out2, decoder_1_out3,
       decoder_1_out4, decoder_1_out5, decoder_1_out6, decoder_1_out7, decoder_1_out9, decoder_1_out10,
       decoder_1_out11, decoder_1_out12, decoder_1_out13, decoder_1_out14, decoder_1_out15, E_out, F_out,
       G_out;

  Decoder #(.select(4)) decoder_1 (
    .out0(decoder_1_out0), .out1(decoder_1_out1), .out2(decoder_1_out2), .out3(decoder_1_out3),
    .out4(decoder_1_out4), .out5(decoder_1_out5), .out6(decoder_1_out6), .out7(decoder_1_out7),
    .out9(decoder_1_out9), .out10(decoder_1_out10), .out11(decoder_1_out11), .out12(decoder_1_out12),
    .out13(decoder_1_out13), .out14(decoder_1_out14), .out15(decoder_1_out15), .sel(in_1));  // open: out8, en
  nor G (G_out, decoder_1_out0, decoder_1_out1, decoder_1_out7, decoder_1_out12);
  nor F (F_out, decoder_1_out1, decoder_1_out2, decoder_1_out3, decoder_1_out7, decoder_1_out13);
  nor A (A_out, decoder_1_out1, decoder_1_out4, decoder_1_out11, decoder_1_out13);
  nor B (B_out, decoder_1_out5, decoder_1_out6, decoder_1_out11, decoder_1_out12, decoder_1_out14, decoder_1_out15);
  _7_Segment_Display u_7_segment_display_1 (
    .g(G_out), .f(F_out), .a(A_out), .b(B_out), .e(E_out), .d(D_out), .c(C_out));  // open: dp
  nor C (C_out, decoder_1_out2, decoder_1_out12, decoder_1_out14, decoder_1_out15);
  nor D (D_out, decoder_1_out1, decoder_1_out4, decoder_1_out7, decoder_1_out9, decoder_1_out10, decoder_1_out15);
  nor E (E_out, decoder_1_out1, decoder_1_out3, decoder_1_out4, decoder_1_out5, decoder_1_out7, decoder_1_out9);

  // Notes on the sheet:
  //   Jeśli wyświetlanie wartości od 0 do F jest błędne (w poleceniu jest od 0 do 9) to byłbym wdzięczny za komentarz :) )
endmodule
