// Logisim project MajchrowskiMateusz.circ as structural Verilog: 1 circuit, main circuit main
module main (
  input  C,
  input  B,
  input  A,
  output out_4,
  output out_5,
  output out_6
);

  wire and_1_out, and_2_out, nand_1_out, nand_2_out, nand_3_out, nand_4_out, nand_5_out, nand_6_out,
       nand_7_out, nand_8_out, nor_1_out, nor_2_out, nor_3_out, nor_4_out, nor_5_out, nor_6_out, nor_7_out,
       nor_8_out, nor_9_out, nor_10_out, nor_11_out;

  and and_1 (and_1_out, C, B, ~A);  // AND_Gate
  and and_2 (and_2_out, C, ~B, A);  // AND_Gate
  nand nand_1 (nand_1_out, C, B);
  nand nand_2 (nand_2_out, A, A);
  nand nand_3 (nand_3_out, C, A);
  nand nand_4 (nand_4_out, B, B);
  nor nor_1 (nor_1_out, C, C);
  nor nor_2 (nor_2_out, B, B);
  nor nor_3 (nor_3_out, C, C);
  nor nor_4 (nor_4_out, A, A);
  nand nand_5 (nand_5_out, nand_1_out, nand_1_out);
  nand nand_6 (nand_6_out, nand_3_out, nand_3_out);
  or or_1 (out_4, and_1_out, and_2_out);
  nor nor_5 (nor_5_out, nor_1_out, nor_2_out);
  nor nor_6 (nor_6_out, nor_5_out, nor_5_out);
  nor nor_7 (nor_7_out, nor_8_out, nor_8_out);
  nor nor_8 (nor_8_out, nor_3_out, nor_4_out);
  nand nand_7 (nand_7_out, nand_5_out, nand_2_out);
  nand nand_8 (nand_8_out, nand_6_out, nand_4_out);
  nor nor_9 (nor_9_out, nor_6_out, A);
  nor nor_10 (nor_10_out, nor_7_out, B);
  nand nand_9 (out_6, nand_7_out, nand_8_out);
  nor nor_11 (nor_11_out, nor_9_out, nor_10_out);
  nor nor_12 (out_5, nor_11_out, nor_11_out);

  // Notes on the sheet:
  //   Numer zestawu = 608
  //    c 1 1 1 1 0 0 0 0
  //    b 1 1 0 0 1 1 0 0
  //   a 1 0 1 0 1 0 1 0
  //   Q 0 1 1 0 0 0 0 0
endmodule
