// Logisim project MajchrowskiMateusz138.circ as structural Verilog: 1 circuit, main circuit main
module main (
  input  nE1,
  input  nE2,
  input  E3,
  input  A2,
  input  A1,
  input  A0,
  output nY0,
  output nY1,
  output nY2,
  output nY3,
  output nY4,
  output nY5,
  output nY6,
  output nY7
);

  wire nand_1_out, nor_1_out, nor_2_out, nor_3_out, nor_4_out, nor_5_out, nor_6_out, nor_7_out, nor_8_out,
       nor_9_out, nor_10_out, nor_11_out, nor_12_out, nor_13_out, nor_14_out, nor_15_out, nor_16_out,
       nor_17_out, nor_18_out, nor_19_out, nor_20_out, nor_21_out, nor_22_out, nor_23_out, nor_24_out,
       nor_25_out, nor_26_out, nor_27_out, nor_28_out, nor_29_out, nor_30_out, nor_31_out, nor_32_out,
       nor_33_out, nor_34_out, nor_35_out, nor_36_out, nor_37_out, nor_38_out, nor_39_out, nor_40_out,
       not_1_out, not_2_out, not_3_out, not_4_out, not_6_out, not_7_out;

  not not_1 (not_1_out, A2);
  not not_2 (not_2_out, not_1_out);
  nor nor_1 (nor_1_out, not_2_out, not_7_out);
  nor nor_2 (nor_2_out, nor_1_out, nor_1_out);
  not not_3 (not_3_out, A1);
  not not_4 (not_4_out, not_3_out);
  nor nor_3 (nor_3_out, not_4_out, nand_1_out);
  nor nor_4 (nor_4_out, nor_3_out, nor_3_out);
  nor nor_5 (nor_5_out, nor_2_out, nor_4_out);
  not not_5 (nY0, nor_5_out);
  not not_6 (not_6_out, A0);
  not not_7 (not_7_out, not_6_out);
  nor nor_6 (nor_6_out, nand_1_out, not_4_out);
  nor nor_7 (nor_7_out, not_2_out, not_6_out);
  nor nor_8 (nor_8_out, nor_6_out, nor_6_out);
  nor nor_9 (nor_9_out, nor_7_out, nor_7_out);
  nor nor_10 (nor_10_out, nor_8_out, nor_9_out);
  not not_8 (nY1, nor_10_out);
  nor nor_11 (nor_11_out, nand_1_out, not_7_out);
  nor nor_12 (nor_12_out, nor_11_out, nor_11_out);
  nor nor_13 (nor_13_out, nor_12_out, nor_17_out);
  not not_9 (nY2, nor_13_out);
  nor nor_14 (nor_14_out, not_2_out, not_3_out);
  nor nor_15 (nor_15_out, nand_1_out, not_2_out);
  nor nor_16 (nor_16_out, nor_15_out, nor_15_out);
  nor nor_17 (nor_17_out, nor_14_out, nor_14_out);
  nor nor_18 (nor_18_out, not_3_out, not_6_out);
  nor nor_19 (nor_19_out, nor_18_out, nor_18_out);
  nor nor_20 (nor_20_out, nor_16_out, nor_19_out);
  not not_10 (nY3, nor_20_out);
  nand nand_1 (nand_1_out, ~nE1, ~nE2, E3);  // NAND_Gate
  nor nor_21 (nor_21_out, nand_1_out, not_1_out);
  nor nor_22 (nor_22_out, nor_21_out, nor_21_out);
  nor nor_23 (nor_23_out, nor_22_out, nor_27_out);
  not not_11 (nY4, nor_23_out);
  nor nor_24 (nor_24_out, not_4_out, not_7_out);
  nor nor_25 (nor_25_out, nand_1_out, not_1_out);
  nor nor_26 (nor_26_out, nor_25_out, nor_25_out);
  nor nor_27 (nor_27_out, nor_24_out, nor_24_out);
  nor nor_28 (nor_28_out, not_4_out, not_6_out);
  nor nor_29 (nor_29_out, nor_28_out, nor_28_out);
  nor nor_30 (nor_30_out, nor_26_out, nor_29_out);
  not not_12 (nY5, nor_30_out);
  nor nor_31 (nor_31_out, nand_1_out, not_1_out);
  nor nor_32 (nor_32_out, not_3_out, not_7_out);
  nor nor_33 (nor_33_out, nor_32_out, nor_32_out);
  nor nor_34 (nor_34_out, nor_31_out, nor_31_out);
  nor nor_35 (nor_35_out, nor_34_out, nor_33_out);
  not not_13 (nY6, nor_35_out);
  nor nor_36 (nor_36_out, nand_1_out, not_1_out);
  nor nor_37 (nor_37_out, nor_36_out, nor_36_out);
  nor nor_38 (nor_38_out, nor_37_out, nor_40_out);
  not not_14 (nY7, nor_38_out);
  nor nor_39 (nor_39_out, not_3_out, not_6_out);
  nor nor_40 (nor_40_out, nor_39_out, nor_39_out);
endmodule
